# Fritzing sketch fritzing_schematic (saved by Fritzing 0.9.10b)
breadboards: 1

parts:
  Part1 = Arduino Uno (Rev3)
  LED1 = LED - 5mm [color="Green (555nm)" current=0.030 package="5 mm [THT]"]
  S1 = Pushbutton [package="[THT]"]
  R1 = Resistor [tolerance=±1% power=0.25 resistance=220 package=THT]
  R2 = Resistor [tolerance=±1% power=0.25 resistance=10k package=THT]

nets:
  N1: Part1.D13/SCK, LED1.anode
  N2: Part1.D2, S1.Pin_1, S1.Pin_2, R2.Pin_1
  N3: Part1.5V, S1.Pin_3, S1.Pin_4
  N4: Part1.GND, R1.Pin_0, R2.Pin_0
  N5: LED1.cathode, R1.Pin_1
