# Fritzing sketch fritzing_schematic (saved by Fritzing 1.0.3b)
breadboards: 1

parts:
  Part1 = Arduino Uno (Rev3)
  LED1 = LED - 5mm [color="Green (555nm)" current=0.030 package="5 mm [THT]"]
  R1 = Resistor [tolerance=±1% power=0.25 resistance=220 package=THT]
  S1 = Pushbutton [package="[THT]"]
  S2 = Pushbutton [package="[THT]"]

nets:
  N1: Part1.D12/MISO, S1.Pin_1, S1.Pin_2
  N2: Part1.D13/SCK, S2.Pin_1, S2.Pin_2
  N3: Part1.D2, LED1.anode
  N4: Part1.GND, R1.Pin_1, S1.Pin_3, S1.Pin_4, S2.Pin_3, S2.Pin_4
