# Fritzing sketch fritzing_schematic (saved by Fritzing 1.0.3b)
breadboards: 1

parts:
  Part1 = Arduino Uno (Rev3)
  R1 = Resistor [tolerance=±1% power=0.25 resistance=220 package=THT]
  LED1 = smd LED [color="Green (555nm)" current=30mA package="0805 [SMD]"]
  LED2 = smd LED [color="Green (555nm)" current=30mA package="0805 [SMD]"]
  LED3 = smd LED [color="Green (555nm)" current=30mA package="0805 [SMD]"]
  LED4 = smd LED [color="Green (555nm)" current=30mA package="0805 [SMD]"]
  R2 = Resistor [tolerance=±1% power=0.25 resistance=220 package=THT]
  R3 = Resistor [tolerance=±1% power=0.25 resistance=220 package=THT]
  R4 = Resistor [tolerance=±1% power=0.25 resistance=220 package=THT]

nets:
  N1: Part1.D8, LED4.anode
  N2: Part1.D2, LED1.anode
  N3: Part1.D4, LED2.anode
  N4: Part1.D7, LED3.anode
  N5: Part1.GND, R1.Pin_1, R2.Pin_1, R3.Pin_1, R4.Pin_1
  N6: R1.Pin_0, LED1.cathode
  N7: LED2.cathode, R2.Pin_0
  N8: LED3.cathode, R3.Pin_0
  N9: LED4.cathode, R4.Pin_0
