# Fritzing sketch RGB_led (saved by Fritzing 1.0.3b)
breadboards: 1

parts:
  Part1 = Arduino Uno (Rev3)
  R2 = Resistor [tolerance=±5% power=0.25W resistance=220 package=THT]
  R3 = Resistor [tolerance=±5% power=0.25W resistance=220 package=THT]
  R4 = Resistor [tolerance=±5% power=0.25W resistance=220 package=THT]
  LED1 = RGB LED - (4 legs) [color="Red (633nm)" current=0.030A package="5 mm [THT]"]

nets:
  N1: Part1.D9_PWM, R4.Pin_1
  N2: Part1.D10_PWM/SS, R3.Pin_1
  N3: Part1.D11_PWM/MOSI, R2.Pin_1
  N4: Part1.GND, LED1.common_anode
  N5: R2.Pin_0, LED1.red_cathode
  N6: R3.Pin_0, LED1.green_cathode
  N7: R4.Pin_0, LED1.blue_cathode
