# Fritzing sketch photoresistor (saved by Fritzing 1.0.3b)
breadboards: 1

parts:
  Part1 = Arduino Uno (Rev3)
  R2 = Resistor [tolerance=±5% power=0.25W resistance=10k package=THT]
  R3 = Photocell (LDR) [power=0.25W dark_resistance_@0.01lx=300kΩ light_resistance_@100lx=400Ω luminance=10lx package=THT]

nets:
  N1: Part1.A0, R2.Pin_0, R3.pin_1
  N2: Part1.5V, R2.Pin_1
  N3: Part1.GND, R3.pin_0
