# Fritzing sketch seven_segment_display (saved by Fritzing 1.0.3b)
breadboards: 1

parts:
  Part1 = Arduino Uno (Rev3)
  DI1 = 7-Segment LED Display [package=THT]
  R1 = Resistor [tolerance=±5% power=0.25W resistance=1k package=THT]

nets:
  N1: Part1.D8, DI1.cathodeC
  N2: Part1.D2, DI1.cathodeG
  N3: Part1.D3_PWM, DI1.cathodeF
  N4: Part1.D4, DI1.cathodeA
  N5: Part1.D5_PWM, DI1.cathodeB
  N6: Part1.D6_PWM, DI1.cathodeE
  N7: Part1.D7, DI1.cathodeD
  N8: Part1.GND, R1.Pin_1
  N9: DI1.commAnode, R1.Pin_0
